// Logisim project part1.circ as structural Verilog: 8 circuits, main circuit MyTest
module MyTest (
);

  wire mux2to1_1_out_4, mux4to1_1_out_6, undriven;

  NAND1 nand1_1 ();  // open: in_1, in_2, out_3
  Mux2to1 mux2to1_1 (.in_1(1'b1), .in_2(1'b1), .in_3(1'b1), .out_4(mux2to1_1_out_4));
  Dec2to4 dec2to4_1 ();  // open: in_1, out_2
  NegSign negsign_1 ();  // open: in_1, out_2
  // Probe on mux2to1_1_out_4
  NOR1 nor1_1 ();  // open: in_1, in_2, out_3
  XOR1 xor1_1 ();  // open: in_1, in_2, out_3
  Mux4to1 mux4to1_1 (.in_1(1'b1), .in_2(1'b1), .in_3(1'b1), .in_4(1'b1), .in_5(2'b11), .out_6(mux4to1_1_out_6));
  // Probe on mux4to1_1_out_6
  // Probe on undriven
endmodule

module NAND1 (
  input  in_1,
  input  in_2,
  output out_3
);

  wire and_1_out;

  and and_1 (and_1_out, in_1, in_2);
  not not_1 (out_3, and_1_out);

  // Other names for the same wires on the sheet: Result = out_3; X = in_1; Y = in_2

  // Notes on the sheet:
  //   ------------------------------------------ Put your circuit below this line ------------------
endmodule

module NOR1 (
  input  in_1,
  input  in_2,
  output out_3
);

  wire or_1_out;

  not not_1 (out_3, or_1_out);
  or or_1 (or_1_out, in_1, in_2);

  // Other names for the same wires on the sheet: Result = out_3; X = in_1; Y = in_2

  // Notes on the sheet:
  //   ------------------------------------------ Put your circuit below this line ------------------
endmodule

module XOR1 (
  input  in_1,
  input  in_2,
  output out_3
);

  wire and_1_out, and_2_out, not_1_out, not_2_out;

  not not_1 (not_1_out, in_1);
  not not_2 (not_2_out, in_2);
  and and_1 (and_1_out, in_2, not_1_out);
  and and_2 (and_2_out, not_2_out, in_1);
  or or_1 (out_3, and_1_out, and_2_out);

  // Other names for the same wires on the sheet: Result = out_3; X = in_1; Y = in_2

  // Notes on the sheet:
  //   ------------------------------------------ Put your circuit below this line ------------------
endmodule

module Mux2to1 (
  input  in_1,
  input  in_2,
  input  in_3,
  output out_4
);

  wire and_1_out, and_2_out, not_1_out;

  not not_1 (not_1_out, in_3);
  and and_1 (and_1_out, in_1, not_1_out);
  and and_2 (and_2_out, in_2, in_3);
  or or_1 (out_4, and_1_out, and_2_out);

  // Other names for the same wires on the sheet: Result = out_4; S = in_3; X = in_1; Y = in_2

  // Notes on the sheet:
  //   ------------------------------------------ Put your circuit below this line ------------------
endmodule

module Dec2to4 (
  input  [1:0] in_1,
  output [3:0] out_2
);

  wire not_1_out, not_2_out;

  not not_1 (not_1_out, in_1[0]);
  not not_2 (not_2_out, in_1[1]);
  and and_1 (out_2[0], not_1_out, not_2_out);
  and and_2 (out_2[1], in_1[0], not_2_out);
  and and_3 (out_2[2], not_1_out, in_1[1]);
  and and_4 (out_2[3], in_1[1], in_1[0]);

  // Other names for the same wires on the sheet: Result[3:0] = out_2; S[1:0] = in_1

  // Notes on the sheet:
  //   S is decoder's 2-bit inputs
  //   ------------------------------------------ Put your circuit below this line ------------------
  //   Result is decoder's 4-bit outputs
endmodule

module Mux4to1 (
  input  in_1,
  input  in_2,
  input  in_3,
  input  in_4,
  input  [1:0] in_5,
  output out_6
);

  wire and_1_out, and_2_out, and_3_out, and_4_out, and_5_out, and_6_out, not_1_out, not_2_out, not_3_out,
       or_1_out, or_2_out;

  not not_1 (not_1_out, in_5[0]);
  not not_2 (not_2_out, in_5[0]);
  and and_1 (and_1_out, in_1, in_5[0]);
  and and_2 (and_2_out, not_1_out, in_2);
  and and_3 (and_3_out, in_3, in_5[0]);
  and and_4 (and_4_out, not_2_out, in_4);
  or or_1 (or_1_out, and_1_out, and_2_out);
  or or_2 (or_2_out, and_3_out, and_4_out);
  and and_5 (and_5_out, or_1_out, in_5[1]);
  not not_3 (not_3_out, in_5[1]);
  and and_6 (and_6_out, not_3_out, or_2_out);
  or or_3 (out_6, and_5_out, and_6_out);

  // Other names for the same wires on the sheet: A = in_1; B = in_2; C = in_3; D = in_4; Result = out_6;
  //   S[1:0] = in_5

  // Notes on the sheet:
  //   S=00 selects A
  //   S=01 selects B
  //   S=10 selects C
  //   S=11 selects D
  //   ------------------------------------------ Put your circuit below this line ------------------
endmodule

module NegSign (
  input  [7:0] in_1,
  output [7:0] out_2
);

  not not_1 (out_2[7], in_1[7]);

  assign out_2[6:0] = in_1[6:0];

  // Other names for the same wires on the sheet: Result[7:0] = {out_2[7], in_1[6:0]}; X[7:0] = in_1

  // Notes on the sheet:
  //   ------------------------------------------ Put your circuit below this line ------------------
endmodule
