// Logisim project shr.circ as structural Verilog
module shr (
  input  [7:0] In_A,
  input  [2:0] In_B,
  output [7:0] R
);


  // Other names for the same wires on the sheet: A[7:0] = In_A; B[2:0] = In_B; Result[7:0] = R

  // Notes on the sheet:
  //   ------------------------- Put your circuit below this line ------------------
endmodule
