// Logisim project FSM_test.circ as structural Verilog: 1 circuit, main circuit main
module main (
  output out_1,
  output out_2,
  output out_3,
  output halt,
  output Next_st1,
  output Next_st0
);

  wire clock_1_out;
  wire [3:0] adder_1_out;

  Clock clock_1 (.out(clock_1_out));
  Adder #(.width(4)) adder_1 (.a(4'b0001), .b({halt, out_3, out_2, out_1}), .out(adder_1_out));  // open: cin, cout
  Register #(.width(4)) register_1 (
    .D(adder_1_out), .clk(clock_1_out), .Q({halt, out_3, out_2, out_1}));  // open: en, clr
  StateBitOne statebitone_1 (.Next_State_Bit_1(Next_st1), .FSM_Input(out_1), .State_Bit_0(out_2), .State_Bit_1(out_3));
  StateBitZero statebitzero_1 (
    .Next_State_Bit_0(Next_st0), .FSM_Input(out_1), .State_Bit_0(out_2), .State_Bit_1(out_3));

  // Other names for the same wires on the sheet: FSM_In = out_1; St0 = out_2; St1 = out_3
endmodule
