// Logisim project mux2to1_test.circ as structural Verilog: 1 circuit, main circuit main
module main (
  output out_1,
  output out_2,
  output out_3,
  output halt,
  output out_5
);

  wire clock_1_out;
  wire [3:0] adder_1_out;

  Clock clock_1 (.out(clock_1_out));
  Adder #(.width(4)) adder_1 (.a(4'b0001), .b({halt, out_3, out_2, out_1}), .out(adder_1_out));  // open: cin, cout
  Register #(.width(4)) register_1 (
    .D(adder_1_out), .clk(clock_1_out), .Q({halt, out_3, out_2, out_1}));  // open: en, clr
  Mux2to1 mux2to1_1 (.in_1(out_1), .in_2(out_2), .in_3(out_3), .out_4(out_5));

  // Other names for the same wires on the sheet: In_X = out_1; In_Y = out_2; In_S = out_3
endmodule
