// Logisim project nand_nor_xor_test.circ as structural Verilog: 1 circuit, main circuit main
module main (
  output out_1,
  output out_2,
  output halt,
  output out_4,
  output out_5,
  output out_6
);

  wire clock_1_out;
  wire [2:0] adder_1_out;

  Clock clock_1 (.out(clock_1_out));
  Adder #(.width(3)) adder_1 (.a(3'b001), .b({halt, out_2, out_1}), .out(adder_1_out));  // open: cin, cout
  Register #(.width(3)) register_1 (.D(adder_1_out), .clk(clock_1_out), .Q({halt, out_2, out_1}));  // open: en, clr
  NAND1 nand1_1 (.in_1(out_1), .in_2(out_2), .out_3(out_4));
  NOR1 nor1_1 (.in_1(out_1), .in_2(out_2), .out_3(out_5));
  XOR1 xor1_1 (.in_1(out_1), .in_2(out_2), .out_3(out_6));

  // Other names for the same wires on the sheet: In_A = out_1; In_B = out_2
endmodule
