// Logisim project negsign_test.circ as structural Verilog: 1 circuit, main circuit main
module main (
  output [7:0] out_1,
  output [7:0] out_2,
  output halt
);

  wire clock_1_out;
  wire [8:0] adder_1_out;

  Register #(.width(9)) register_1 (.D(adder_1_out), .clk(clock_1_out), .Q({halt, out_1}));  // open: en, clr
  Clock clock_1 (.out(clock_1_out));
  Adder #(.width(9)) adder_1 (.a(9'h1), .b({halt, out_1}), .out(adder_1_out));  // open: cin, cout
  NegSign negsign_1 (.in_1(out_1), .out_2(out_2));
endmodule
