// Logisim project shr_test.circ as structural Verilog: 1 circuit, main circuit main
module main (
  output [7:0] out_1,
  output [2:0] out_2,
  output halt,
  output [7:0] out_4
);

  wire clock_1_out;
  wire [11:0] adder_1_out;

  Clock clock_1 (.out(clock_1_out));
  Adder #(.width(12)) adder_1 (.a(12'h1), .b({halt, out_2, out_1}), .out(adder_1_out));  // open: cin, cout
  Register #(.width(12)) register_1 (.D(adder_1_out), .clk(clock_1_out), .Q({halt, out_2, out_1}));  // open: en, clr
  // shr shr_1: pin names not known; wires that end beside it: out_2, out_1, out_4

  // Other names for the same wires on the sheet: A[7:0] = out_1; B[2:0] = out_2; Result[7:0] = out_4
endmodule
